# Fritzing sketch Untitled Sketch 2 (saved by Fritzing 0.9.3b)
breadboards: 1

parts:
  Part_1 = Weather Shield [part_number=DEV-12081]
  Part1 = Arduino Mega 2560 (Rev3)
  DS1 = DS18B20 1-Wire Temperature Sensor Probe
  Part2 = FC-28 Soil Hygrometer Module
  Part3 = FC-28 Soil Hygrometer Module - Probe

nets:
  N1: Part_1.RX, Part1.D0_RX0
  N2: Part_1.TX, Part1.D1_TX0
  N3: Part_1.D2, Part1.D2_PWM
  N4: Part_1.D3, Part1.D3_PWM
  N5: Part_1.D4, Part_1.VIN, Part1.D4_PWM
  N6: Part_1.D5, Part1.D5_PWM
  N7: Part_1.D6, Part_1.D11, Part1.D11_PWM, Part1.D6_PWM
  N8: Part_1.D7, Part_1.A4, Part1.A4, Part1.D7_PWM
  N9: Part_1.D8, Part1.D8_PWM
  N10: Part_1.D9, Part_1.A1, Part1.A1, Part1.D9_PWM
  N11: Part_1.D10, Part1.D10_PWM
  N12: Part_1.D12, Part1.D12_PWM
  N13: Part_1.D13, Part1.D13_PWM
  GND: Part_1.GND, Part1.GND, DS1.GND, Part2.GND
  N14: Part_1.SDA, Part1.SDA
  N15: Part_1.SCL, Part1.SCL
  N16: Part_1.A5, Part1.A5
  N17: Part_1.A3, Part1.A3
  N18: Part_1.A2, Part1.A2
  N19: Part_1.A0, Part1.A0
  N20: Part1.A6, Part2.AO
  5V: Part1.5V, DS1.VDD, Part2.VCC
  N21: Part1.D22, DS1.DQ
  N22: Part2.POS, Part3.POS
  N23: Part2.NEG, Part3.NEG

custom parts:
  Weather Shield: Weather Shield includes: - ALS-PT19 Light Sensor - HTU21D Humidity Sensor - MPL3115A2 - TEMT6000 Check out the product page on www.sparkfun.com for documentation!
  FC-28 Soil Hygrometer Module: The FC-28 is a soil hygrometer module that uses the Texas Instruments LM393 comparator chip to provide an analog measurement of soil humidity. The digital output is high when soil moisture is over a certain threshold, as determined by adjusting the potentiometer.
  FC-28 Soil Hygrometer Module - Probe: The FC-28 is a soil hygrometer module that uses the Texas Instruments LM393 comparator chip to provide an analog measurement of soil humidity.
